// Logisim project 2-1MUX.circ as structural Verilog: 1 circuit, main circuit main
module main (
  input  D0,
  input  D1,
  input  S,
  output Y
);

  // AND_Gate and_1 is placed but not wired
  // AND_Gate and_2 is placed but not wired
  // NOT_Gate not_1 is placed but not wired
  // OR_Gate or_1 is placed but not wired
endmodule
