// Logisim project Decoder3to8.circ as structural Verilog: 1 circuit, main circuit main
module main (
  input  A,
  input  G1,
  input  B,
  input  G2A_L,
  input  C,
  input  G2B_L,
  output Y0_L,
  output Y4_L,
  output Y1_L,
  output Y5_L,
  output Y2_L,
  output Y6_L,
  output Y3_L,
  output Y7_L
);


  // Notes on the sheet:
  //   G1: pull=down
  //   G2B_L: pull=down
  //   G2A_L: pull=down
  //   3线-8线译码器：74LS138（低电平译码）
  //   请不要改变封装外观，否则无法完成测试
endmodule
