// Logisim project IFU.circ as structural Verilog: 2 circuits, main circuit IFU
module InstrToImm (
  input  [31:0] Instr,
  input  [2:0] Extop,
  output [31:0] imm
);

  wire [11:0] bit_extender_4_out;
  wire [19:0] bit_extender_1_out, bit_extender_2_out, bit_extender_3_out;

  assign bit_extender_1_out = {{19{Instr[31]}}, Instr[31]};  // Bit_Extender bit_extender_1
  assign bit_extender_2_out = {{19{Instr[31]}}, Instr[31]};  // Bit_Extender bit_extender_2
  assign bit_extender_3_out = {{19{Instr[31]}}, Instr[31]};  // Bit_Extender bit_extender_3
  assign bit_extender_4_out = {{11{Instr[31]}}, Instr[31]};  // Bit_Extender bit_extender_4
  Multiplexer #(.select(3), .width(32), .enable("false")) multiplexer_1 (
    .in0({bit_extender_1_out, Instr[31:20]}), .in1({Instr[31:12], {12{1'b0}}}),
    .in2({bit_extender_2_out, Instr[31:25], Instr[11:7]}),
    .in3({bit_extender_3_out, Instr[7], Instr[30:25], Instr[11:8], 1'b0}),
    .in4({bit_extender_4_out, Instr[19:12], Instr[20], Instr[30:21], 1'b0}), .in5({32{1'b0}}),
    .in6({32{1'b0}}), .in7({32{1'b0}}), .out(imm), .sel(Extop));

  // Notes on the sheet:
  //   Instr: pull=down
  //   Extop: pull=down
  //   I
  //   U
  //   S
  //   B
  //   J
  //   输入引脚
  //   输出引脚
endmodule

module IFU (
  input  [31:0] Imm,
  input  Branch,
  input  clk,
  input  Jump,
  input  ZERO,
  input  [2:0] ExtOp,
  output [31:0] Instr,
  output [6:0] opcode,
  output [4:0] rs2,
  output [4:0] rs1,
  output [4:0] rd,
  output [2:0] funct3,
  output [6:0] funct7,
  output [31:0] Imm_2
);

  wire and_1_out, or_1_out, RESET;
  wire [31:0] adder_1_out, multiplexer_1_out, PC_q;

  Register #(.width(32), .trigger("falling"), .Select("low")) PC (
    .D(adder_1_out), .Q(PC_q), .clk(clk), .clr(RESET));  // open: en
  and and_1 (and_1_out, ZERO, Branch);
  Button u_RESET (.out(RESET));
  Multiplexer #(.width(32), .enable("false")) multiplexer_1 (
    .in0(32'h4), .in1(Imm), .out(multiplexer_1_out), .sel(or_1_out));
  or or_1 (or_1_out, Jump, and_1_out);
  // Probe on multiplexer_1_out
  InstrToImm InstrToImm (.Instr({funct7, Instr[24:15], funct3, Instr[11:0]}), .Extop(ExtOp), .imm(Imm_2));
  Adder #(.width(32)) adder_1 (.a(PC_q), .b(multiplexer_1_out), .out(adder_1_out));  // open: cin, cout
  ROM #(.addrWidth(12), .dataWidth(32), .Select("low")) rom_1 (
    .addr(PC_q[13:2]), .data({funct7, Instr[24:15], funct3, Instr[11:0]}));

  assign {Instr[31:25], Instr[14:12]} = {funct7, funct3};
  assign opcode = Instr[6:0];
  assign rd = Instr[24:20];
  assign rs1 = Instr[11:7];
  assign rs2 = Instr[19:15];

  // Notes on the sheet:
  //   Imm: pull=down
  //   ZERO: pull=down
  //   Jump: pull=down
  //   Branch: pull=down
  //   指令解析
  //   因为存储器大小限制，地址位设置为10位，同时由于指令字长32位，地址最低2位截除。
  //   注意，这里的存储器请按照讲义使用ROM，如果使用RAM会导致评测出错！
  //   注意，这里的时钟信号请使用引脚，否则会导致评测出错！
  //   输入信号
  //   不考虑低2位
  //   输出信号
endmodule
