// Logisim project cmos_or.circ as structural Verilog: 1 circuit, main circuit cmos_or
module cmos_or (
  input  X,
  input  Y,
  output Z
);


  // Notes on the sheet:
  //   或门实现电路
endmodule
