// Logisim project cmos_or_tst.circ as structural Verilog: 1 circuit, main circuit test
module test (
  output [3:0] Cnt,
  output [1:0] XY,
  output F,
  output _passed,
  output halt
);

  wire CLK, FS, Running;

  Clock clock_1 (.out(CLK));
  Counter #(.width(4), .max('hf), .behavior("old")) counter_1 (
    .count(Running), .Q(Cnt), .clk(CLK));  // open: load, D, carry, clr, preset
  // Probe on Cnt
  // Probe on Cnt
  // Probe on 4'b0011
  Comparator #(.width(4)) comparator_1 (.a(Cnt), .b(4'b0011), .eq(halt));  // open: gt, lt
  ROM #(.addrWidth(4), .dataWidth(2), .Select("high")) rom_1 (.addr(Cnt), .data(XY));
  ROM #(.addrWidth(4), .dataWidth(1), .Select("high")) rom_2 (.addr(Cnt), .data(FS));
  not not_1 (Running, halt);
  RAM #(.addrWidth(4), .dataWidth(1), .bus("separate"), .Select("low")) ram_1 (
    .addr(Cnt), .din(F), .str(Running), .clk(CLK));  // open: data, sel, ld, clr
  cmos_or cmos_or_1 (.X(XY[0]), .Y(XY[1]), .Z(F));
  xnor xnor_1 (_passed, F, FS);
  Pull_Resistor pull_resistor_1 (.node(_passed));

  // Other names for the same wires on the sheet: Equal = _passed; tunnel[3:0] = Cnt

  // Notes on the sheet:
  //   测试节拍数
  //   contents of rom_1 (hex, n*v repeats v):
  //   0 1 2 3
  //   contents of rom_2 (hex, n*v repeats v):
  //   0 1 1 1
endmodule
