// Logisim project lab1.1.circ as structural Verilog: 1 circuit, main circuit main
// Truth
module main (
  input  X,
  input  Y,
  input  Z,
  output F
);


  // Notes on the sheet:
  //   输入引脚
  //   请勿增加、删除引脚，用隧道标签构建电路，
  //   3输入多数表决器电路
  //   请勿更改电路封装外观。
  //   输出引脚
endmodule
