// Logisim project lab1.2.circ as structural Verilog: 1 circuit, main circuit cmos_or
module cmos_or (
  input  X,
  input  Y,
  output Z
);

  wire transistor_1_out, transistor_2_out, transistor_3_out, transistor_4_out;

  Transistor transistor_1 (.in(transistor_4_out), .out(transistor_1_out), .gate(X));
  Transistor transistor_2 (.in(transistor_1_out), .out(transistor_2_out), .gate(Y));
  Transistor #(.\type ("n")) transistor_3 (.in(transistor_2_out), .out(transistor_3_out), .gate(X));
  Transistor transistor_4 (.in(Z), .out(transistor_4_out), .gate(transistor_2_out));
  Transistor #(.\type ("n")) transistor_5 (.in(transistor_3_out), .out(Z), .gate(transistor_2_out));
  Transistor #(.\type ("n")) transistor_6 (.in(transistor_2_out), .out(transistor_3_out), .gate(Y));
  // also tied to GND on the sheet: transistor_3_out
  // also tied to VCC on the sheet: transistor_4_out

  // Notes on the sheet:
  //   输入引脚
  //   请勿增加、删除引脚，用隧道标签构建电路
  //   请勿更改电路封装外观
  //   提示：使用三极管组件实现或门电路，禁止直接使用逻辑门组件。
  //   输出引脚
endmodule
