// Logisim project lab2.1.circ as structural Verilog: 1 circuit, main circuit main
module main (
  input  G1,
  input  G2A_L,
  input  G2B_L,
  input  A,
  input  B,
  input  C,
  output Y0_L,
  output Y1_L,
  output Y2_L,
  output Y3_L,
  output Y4_L,
  output Y5_L,
  output Y6_L,
  output Y7_L
);

  wire and_1_out, not_1_out, not_2_out, not_3_out;

  and and_1 (and_1_out, G1, ~G2A_L, ~G2B_L);  // AND_Gate
  not not_1 (not_1_out, A);
  not not_2 (not_2_out, B);
  not not_3 (not_3_out, C);
  nand nand_1 (Y0_L, and_1_out, not_1_out, not_2_out, not_3_out);
  nand nand_2 (Y1_L, and_1_out, A, not_2_out, not_3_out);
  nand nand_3 (Y2_L, and_1_out, not_1_out, B, not_3_out);
  nand nand_4 (Y3_L, and_1_out, A, B, not_3_out);
  nand nand_5 (Y4_L, and_1_out, not_1_out, not_2_out, C);
  nand nand_6 (Y5_L, and_1_out, A, not_2_out, C);
  nand nand_7 (Y6_L, and_1_out, not_1_out, B, C);
  nand nand_8 (Y7_L, and_1_out, A, B, C);

  // Notes on the sheet:
  //   输入引脚
  //   请勿修改引脚名称、电路名称及电路封装外观
  //   提示：使用独立逻辑门实现3-8译码器，禁止直接使用译码器组件。
  //   输出引脚
endmodule
