// Logisim project lab2.2.circ as structural Verilog: 1 circuit, main circuit main
module main (
  input  I0,
  input  I1,
  input  I2,
  input  I4,
  input  I5,
  input  I3,
  input  I6,
  input  I7,
  output O0,
  output O1,
  output O2
);

  wire nand_1_out, nand_2_out, nand_3_out, nand_4_out, nand_5_out, nand_6_out, nand_7_out;
  wire [3:3] undriven;

  nand nand_1 (nand_1_out, ~I0, I1);  // NAND_Gate
  nand nand_2 (nand_2_out, ~I0, ~I1, I2);  // NAND_Gate
  nand nand_3 (nand_3_out, ~I0, ~I1, ~I2, I3);  // NAND_Gate
  nand nand_4 (nand_4_out, ~I0, ~I1, ~I2, ~I3, I4);  // NAND_Gate
  nand nand_5 (nand_5_out, ~I0, ~I1, ~I2, ~I3, ~I4, I5);  // NAND_Gate
  nand nand_6 (nand_6_out, ~I0, ~I1, ~I2, ~I3, ~I4, ~I5, I6);  // NAND_Gate
  nand nand_7 (nand_7_out, ~I0, ~I1, ~I2, ~I3, ~I4, ~I5, ~I6, I7);  // NAND_Gate
  nand nand_8 (O1, nand_2_out, nand_3_out, nand_6_out, nand_7_out);
  nand nand_9 (O0, nand_4_out, nand_5_out, nand_6_out, nand_7_out);
  nand nand_10 (O2, nand_1_out, nand_3_out, nand_5_out, nand_7_out);
  Hex_Digit_Display hex_digit_display_1 (.value({undriven[3], O2, O1, O0}));  // open: dp

  // Notes on the sheet:
  //   输入引脚
  //   请勿修改引脚名称、电路名称及电路封装外观
  //   提示：使用独立逻辑门实现8-3优先级编码器，禁止直接使用编码器组件。
  //   输出引脚
endmodule
