// Logisim project lab2.3.circ as structural Verilog: 2 circuits, main circuit main
module main (
  input  [3:0] X,
  input  [3:0] Y,
  input  Cin,
  output [3:0] F,
  output Cout
);

  wire FA0_cout, FA1_cout, FA2_cout;
  wire [3:0] xor_1_out;

  assign xor_1_out = {4{Cin}} ^ Y;  // XOR_Gate xor_1, 4 bits wide
  Hex_Digit_Display hex_digit_display_1 (.value(X));  // open: dp
  FA FA0 (.A(X[0]), .B(xor_1_out[0]), .Cin(Cin), .Cout(FA0_cout), .F(F[0]));
  Hex_Digit_Display hex_digit_display_2 (.value(xor_1_out));  // open: dp
  FA FA1 (.A(X[1]), .B(xor_1_out[1]), .Cin(FA0_cout), .Cout(FA1_cout), .F(F[1]));
  Hex_Digit_Display hex_digit_display_3 (.value(F));  // open: dp
  FA FA2 (.A(X[2]), .B(xor_1_out[2]), .Cin(FA1_cout), .Cout(FA2_cout), .F(F[2]));
  FA FA3 (.A(X[3]), .B(xor_1_out[3]), .Cin(FA2_cout), .Cout(Cout), .F(F[3]));

  // Other names for the same wires on the sheet: SUM[3:0] = F; 操作数x[3:0] = X; 操作数y[3:0] = Y

  // Notes on the sheet:
  //   输入引脚
  //   +
  //   提示：使用独立逻辑门及全加器FA子电路实现4位二进制数加减法器，禁止直接使用加减法器组件。
  //   =
  //   请勿修改引脚名称、电路名称及电路封装外观
  //   输出引脚
endmodule

module FA (
  input  A,
  input  B,
  input  Cin,
  output F,
  output Cout
);

  wire and_1_out, and_2_out, and_3_out, xor_1_out;

  xor xor_1 (xor_1_out, A, B);
  and and_1 (and_1_out, A, B);
  and and_2 (and_2_out, B, Cin);
  and and_3 (and_3_out, A, Cin);
  xor xor_2 (F, xor_1_out, Cin);
  or or_1 (Cout, and_1_out, and_2_out, and_3_out);

  // Notes on the sheet:
  //   全加器
endmodule
