// Logisim project lab3.2.circ as structural Verilog: 1 circuit, main circuit SHRG4U
module SHRG4U (
  input  CLK,
  input  CLR_L,
  input  RIN,
  input  D3,
  input  D2,
  input  D1,
  input  D0,
  input  LIN,
  input  S1,
  input  S0,
  output Q3,
  output Q2,
  output Q1,
  output Q0
);

  wire multiplexer_1_out, multiplexer_2_out, multiplexer_3_out, multiplexer_4_out, not_1_out;

  Multiplexer #(.select(2), .enable("false")) multiplexer_1 (
    .in0(Q3), .in1(Q2), .in2(RIN), .in3(D3), .out(multiplexer_1_out), .sel({S1, S0}));
  Multiplexer #(.select(2), .enable("false")) multiplexer_2 (
    .in0(Q2), .in1(Q1), .in2(Q3), .in3(D2), .out(multiplexer_2_out), .sel({S1, S0}));
  Multiplexer #(.select(2), .enable("false")) multiplexer_3 (
    .in0(Q1), .in1(Q0), .in2(Q2), .in3(D1), .out(multiplexer_3_out), .sel({S1, S0}));
  Multiplexer #(.select(2), .enable("false")) multiplexer_4 (
    .in0(Q0), .in1(LIN), .in2(Q1), .in3(D0), .out(multiplexer_4_out), .sel({S1, S0}));
  D_Flip_Flop #(.trigger("falling")) d_ff_1 (
    .clk(CLK), .D(multiplexer_1_out), .Q(Q3), .reset(not_1_out));  // open: Qn, preset
  D_Flip_Flop #(.trigger("falling")) d_ff_2 (
    .clk(CLK), .D(multiplexer_2_out), .Q(Q2), .reset(not_1_out));  // open: Qn, preset
  D_Flip_Flop #(.trigger("falling")) d_ff_3 (
    .clk(CLK), .D(multiplexer_3_out), .Q(Q1), .reset(not_1_out));  // open: Qn, preset
  D_Flip_Flop #(.trigger("falling")) d_ff_4 (
    .clk(CLK), .D(multiplexer_4_out), .Q(Q0), .reset(not_1_out));  // open: Qn, preset
  not not_1 (not_1_out, CLR_L);

  // Notes on the sheet:
  //   输入引脚
  //   请勿修改引脚名称、电路名称及电路封装外观
  //   提示：使用独立逻辑门实现4位异步清零移位寄存器，禁止直接使用移位寄存器组件。
  //   输出引脚
endmodule
