// Logisim project lab3.5.circ as structural Verilog: 1 circuit, main circuit main
module main (
  input  CLK,
  input  LD,
  input  [3:0] HH1,
  input  [3:0] HH0,
  input  [3:0] MM1,
  input  [3:0] MM0,
  input  [3:0] SS1,
  input  [3:0] SS0,
  output [3:0] HH_H,
  output [3:0] HH_L,
  output [3:0] MM_H,
  output [3:0] MM_L,
  output [3:0] SS_H,
  output [3:0] SS_L,
  output LED_R,
  output LED_G,
  output LED_B,
  output INErr
);

  wire and_1_out, and_2_out, and_4_out, and_5_out, C_H0, C_M0, C_M1, C_S0, C_S1, comparator_1_eq,
       comparator_2_lt, comparator_3_lt, comparator_4_lt, comparator_5_lt, comparator_6_lt, comparator_7_lt,
       comparator_8_lt, comparator_9_eq, comparator_10_gt, LED_EN, nand_1_out, or_1_out, or_2_out, START,
       STOP;
  wire [3:0] cntr4u_3_q0, multiplexer_1_out;

  and and_1 (and_1_out, LD, ~INErr);  // AND_Gate
  CNTR4U cntr4u_1 (
    .CLK(CLK), .LD(and_1_out), .CLR(or_1_out), .Q0(HH_L[0]), .Q1(HH_L[1]), .D0(HH0[0]), .D1(HH0[1]),
    .D2(HH0[2]), .Q2(HH_L[2]), .Q3(HH_L[3]), .D3(HH0[3]), .ENP(C_M1), .ENT(C_M1));  // open: RCO
  or or_1 (or_1_out, C_H0, and_2_out);
  and and_2 (and_2_out, HH_L[0], HH_L[1], C_M1, HH_H[1]);
  CNTR4U cntr4u_2 (
    .CLK(CLK), .LD(and_1_out), .CLR(and_2_out), .Q0(HH_H[0]), .Q1(HH_H[1]), .D0(HH1[0]), .D1(HH1[1]),
    .D2(HH1[2]), .Q2(HH_H[2]), .Q3(HH_H[3]), .D3(HH1[3]), .ENP(C_H0), .ENT(C_H0));  // open: RCO
  Comparator #(.width(4), .mode("unsigned")) comparator_1 (.a(HH1), .b(4'b0010), .eq(comparator_1_eq));  // open: gt, lt
  Comparator #(.width(4), .mode("unsigned")) comparator_2 (.a(HH0), .b(4'b0100), .lt(comparator_2_lt));  // open: gt, eq
  Comparator #(.width(4), .mode("unsigned")) comparator_3 (.a(HH1), .b(4'b0010), .lt(comparator_3_lt));  // open: gt, eq
  Comparator #(.width(4), .mode("unsigned")) comparator_4 (.a(HH0), .b(4'b1010), .lt(comparator_4_lt));  // open: gt, eq
  Comparator #(.width(4), .mode("unsigned")) comparator_5 (.a(MM1), .b(4'b0110), .lt(comparator_5_lt));  // open: gt, eq
  Comparator #(.width(4), .mode("unsigned")) comparator_6 (.a(MM0), .b(4'b1010), .lt(comparator_6_lt));  // open: gt, eq
  Comparator #(.width(4), .mode("unsigned")) comparator_7 (.a(SS1), .b(4'b0110), .lt(comparator_7_lt));  // open: gt, eq
  Comparator #(.width(4), .mode("unsigned")) comparator_8 (.a(SS0), .b(4'b1010), .lt(comparator_8_lt));  // open: gt, eq
  and and_3 (C_H0, HH_L[3], HH_L[0], C_M1);
  and and_4 (and_4_out, comparator_1_eq, comparator_2_lt);
  or or_2 (or_2_out, and_4_out, and_5_out);
  and and_5 (and_5_out, comparator_3_lt, comparator_4_lt);
  CNTR4U cntr4u_3 (
    .CLK(CLK), .LD(LED_EN), .CLR(STOP), .Q0(cntr4u_3_q0[0]), .Q1(cntr4u_3_q0[1]), .D0(1'b1), .D1(1'b0),
    .D2(1'b0), .Q2(cntr4u_3_q0[2]), .Q3(cntr4u_3_q0[3]), .D3(1'b0), .ENP(START), .ENT(START));  // open: RCO
  Multiplexer #(.width(4), .enable("false")) multiplexer_1 (
    .in0(4'b0000), .in1(cntr4u_3_q0), .out({multiplexer_1_out[3], LED_B, multiplexer_1_out[1:0]}), .sel(START));
  Hex_Digit_Display hex_digit_display_1 (.value(HH_H));  // open: dp
  nand nand_1 (nand_1_out, or_2_out, comparator_5_lt, comparator_6_lt, comparator_7_lt, comparator_8_lt);
  and and_6 (INErr, nand_1_out, LD);
  Comparator #(.width(4), .mode("unsigned")) comparator_9 (
    .a(4'b0000), .b(cntr4u_3_q0), .eq(comparator_9_eq));  // open: gt, lt
  not not_1 (START, comparator_9_eq);
  xor xor_1 (LED_R, multiplexer_1_out[0], multiplexer_1_out[1]);
  xor xor_2 (LED_G, multiplexer_1_out[1], LED_B);
  Hex_Digit_Display hex_digit_display_2 (.value(HH_L), .dp(1'b1));
  Hex_Digit_Display hex_digit_display_3 (.value(MM_H));  // open: dp
  CNTR4U cntr4u_4 (
    .CLK(CLK), .LD(and_1_out), .CLR(C_M0), .Q0(MM_L[0]), .Q1(MM_L[1]), .D0(MM0[0]), .D1(MM0[1]), .D2(MM0[2]),
    .Q2(MM_L[2]), .Q3(MM_L[3]), .D3(MM0[3]), .ENP(C_S1), .ENT(C_S1));  // open: RCO
  CNTR4U cntr4u_5 (
    .CLK(CLK), .LD(and_1_out), .CLR(C_M1), .Q0(MM_H[0]), .Q1(MM_H[1]), .D0(MM1[0]), .D1(MM1[1]), .D2(MM1[2]),
    .Q2(MM_H[2]), .Q3(MM_H[3]), .D3(MM1[3]), .ENP(C_M0), .ENT(C_M0));  // open: RCO
  Hex_Digit_Display hex_digit_display_4 (.value(MM_L), .dp(1'b1));
  Hex_Digit_Display hex_digit_display_5 (.value(SS_H));  // open: dp
  and and_7 (C_M0, MM_L[3], MM_L[0], C_S1);
  and and_8 (C_M1, MM_H[2], MM_H[0], C_M0);
  not not_2 (STOP, comparator_10_gt);
  Comparator #(.width(4), .mode("unsigned")) comparator_10 (
    .a(4'b1010), .b(cntr4u_3_q0), .gt(comparator_10_gt));  // open: eq, lt
  Hex_Digit_Display hex_digit_display_6 (.value(SS_L), .dp(1'b1));
  CNTR4U cntr4u_6 (
    .CLK(CLK), .LD(and_1_out), .CLR(C_S0), .Q0(SS_L[0]), .Q1(SS_L[1]), .D0(SS0[0]), .D1(SS0[1]), .D2(SS0[2]),
    .Q2(SS_L[2]), .Q3(SS_L[3]), .D3(SS0[3]), .ENP(1'b1), .ENT(1'b1));  // open: RCO
  CNTR4U cntr4u_7 (
    .CLK(CLK), .LD(and_1_out), .CLR(C_S1), .Q0(SS_H[0]), .Q1(SS_H[1]), .D0(SS1[0]), .D1(SS1[1]), .D2(SS1[2]),
    .Q2(SS_H[2]), .Q3(SS_H[3]), .D3(SS1[3]), .ENP(C_S0), .ENT(C_S0));  // open: RCO
  and and_9 (C_S0, SS_L[3], SS_L[0]);
  and and_10 (C_S1, SS_H[2], SS_H[0], C_S0);
  // RGBLed RGBLED: pin names not known; wires that end beside it: LED_R, LED_G, LED_B
  and and_11 (LED_EN, C_M0, C_M1, C_S0, C_S1);

  // Other names for the same wires on the sheet: H0[3:0] = HH_L; H1[3:0] = HH_H; M0[3:0] = MM_L; M1[3:0] = MM_H;
  //   S0[3:0] = SS_L; S1[3:0] = SS_H

  // Notes on the sheet:
  //   设置初始时间BCD码
  //   输入信号
  //   请勿修改引脚名称、电路名称及电路封装外观
  //   数字时钟
  //   提示：使用4位二进制加法计数器子电路、比较器和独立逻辑门组件实现数字时钟。
  //   在载入有效时，检测设置数据错误
  //   生成三色LED显示信号，持续10个时钟周期
endmodule
