// Logisim project lab3.p1.circ as structural Verilog: 1 circuit, main circuit CNTR4U
module CNTR4U (
  input  CLK,
  input  LD,
  input  CLR,
  input  D0,
  input  D1,
  input  D2,
  input  D3,
  input  ENP,
  input  ENT,
  input  AsyncCLR,
  input  AsyncLD,
  output Q0,
  output Q1,
  output Q2,
  output Q3,
  output RCO
);

  wire and_1_out, and_2_out, and_3_out, and_4_out, and_5_out, and_6_out, and_7_out, and_8_out, and_9_out,
       and_10_out, and_11_out, and_12_out, and_13_out, and_14_out, and_15_out, and_16_out, and_18_out,
       and_19_out, and_20_out, and_21_out, and_22_out, and_23_out, and_24_out, and_25_out, buffer_1_out,
       d_ff_1_qn, d_ff_2_qn, d_ff_3_qn, d_ff_4_qn, not_1_out, not_2_out, not_3_out, or_1_out, or_2_out,
       or_3_out, or_4_out, or_5_out, or_6_out, or_7_out, or_8_out, xor_1_out, xor_2_out, xor_3_out, xor_4_out;

  not not_1 (not_1_out, CLK);
  buf buffer_1 (buffer_1_out, CLR);
  and and_1 (and_1_out, ~d_ff_2_qn, ~d_ff_1_qn);  // AND_Gate
  and and_2 (and_2_out, ~d_ff_3_qn, ~d_ff_2_qn, ~d_ff_1_qn);  // AND_Gate
  not not_2 (not_2_out, d_ff_1_qn);
  and and_3 (and_3_out, not_2_out, and_6_out);
  and and_4 (and_4_out, and_1_out, and_6_out);
  and and_5 (and_5_out, and_2_out, and_6_out);
  and and_6 (and_6_out, ENP, ENT);
  not not_3 (not_3_out, ENT);
  and and_7 (and_7_out, LD, ~buffer_1_out);  // AND_Gate
  and and_8 (and_8_out, ~and_7_out, ~buffer_1_out);  // AND_Gate
  and and_9 (and_9_out, and_7_out, D0);
  and and_10 (and_10_out, and_8_out, xor_1_out);
  xor xor_1 (xor_1_out, and_6_out, ~d_ff_1_qn);  // XOR_Gate
  and and_11 (and_11_out, and_7_out, D1);
  and and_12 (and_12_out, and_8_out, xor_2_out);
  xor xor_2 (xor_2_out, and_3_out, ~d_ff_2_qn);  // XOR_Gate
  and and_13 (and_13_out, and_7_out, D2);
  and and_14 (and_14_out, and_8_out, xor_3_out);
  xor xor_3 (xor_3_out, and_4_out, ~d_ff_3_qn);  // XOR_Gate
  and and_15 (and_15_out, and_7_out, D3);
  and and_16 (and_16_out, and_8_out, xor_4_out);
  xor xor_4 (xor_4_out, and_5_out, ~d_ff_4_qn);  // XOR_Gate
  and and_17 (RCO, ~d_ff_4_qn, ~d_ff_1_qn, ~d_ff_2_qn, ~d_ff_3_qn, ~not_3_out);  // AND_Gate
  or or_1 (or_1_out, and_9_out, and_10_out);
  or or_2 (or_2_out, and_11_out, and_12_out);
  or or_3 (or_3_out, and_13_out, and_14_out);
  or or_4 (or_4_out, and_15_out, and_16_out);
  D_Flip_Flop #(.trigger("falling")) d_ff_1 (
    .clk(not_1_out), .D(or_1_out), .Q(Q0), .Qn(d_ff_1_qn), .preset(and_22_out), .reset(or_5_out));
  or or_5 (or_5_out, AsyncCLR, and_18_out);
  D_Flip_Flop #(.trigger("falling")) d_ff_2 (
    .clk(not_1_out), .D(or_2_out), .Q(Q1), .Qn(d_ff_2_qn), .preset(and_23_out), .reset(or_6_out));
  and and_18 (and_18_out, AsyncLD, ~D0);  // AND_Gate
  or or_6 (or_6_out, AsyncCLR, and_19_out);
  and and_19 (and_19_out, AsyncLD, ~D1);  // AND_Gate
  D_Flip_Flop #(.trigger("falling")) d_ff_3 (
    .clk(not_1_out), .D(or_3_out), .Q(Q2), .Qn(d_ff_3_qn), .preset(and_24_out), .reset(or_7_out));
  or or_7 (or_7_out, AsyncCLR, and_20_out);
  and and_20 (and_20_out, AsyncLD, ~D2);  // AND_Gate
  D_Flip_Flop #(.trigger("falling")) d_ff_4 (
    .clk(not_1_out), .D(or_4_out), .Q(Q3), .Qn(d_ff_4_qn), .preset(and_25_out), .reset(or_8_out));
  or or_8 (or_8_out, AsyncCLR, and_21_out);
  and and_21 (and_21_out, AsyncLD, ~D3);  // AND_Gate
  and and_22 (and_22_out, AsyncLD, D0);
  and and_23 (and_23_out, AsyncLD, D1);
  and and_24 (and_24_out, AsyncLD, D2);
  and and_25 (and_25_out, AsyncLD, D3);

  // Notes on the sheet:
  //   输入引脚
  //   请勿修改引脚名称、电路名称及电路封装外观
  //   提示：使用独立逻辑门实现4位二进制同步计数器，禁止直接使用计数器组件。
  //   输出引脚
endmodule
