// Logisim project lab3.p3.circ as structural Verilog: 1 circuit, main circuit main
module main (
  input  CLK,
  input  LD,
  input  [7:0] seed,
  output [7:0] Dout
);

  wire xor_1_out;

  SHRG4U shrg4u_1 (
    .CLK(CLK), .CLR_L(1'b1), .Q3(Dout[7]), .Q2(Dout[6]), .D3(seed[7]), .D2(seed[6]), .D1(seed[5]),
    .Q1(Dout[5]), .Q0(Dout[4]), .D0(seed[4]), .LIN(Dout[3]), .S1(LD), .S0(1'b1));  // open: RIN
  SHRG4U shrg4u_2 (
    .CLK(CLK), .CLR_L(1'b1), .Q3(Dout[3]), .Q2(Dout[2]), .D3(seed[3]), .D2(seed[2]), .D1(seed[1]),
    .Q1(Dout[1]), .Q0(Dout[0]), .D0(seed[0]), .LIN(xor_1_out), .S1(LD), .S0(1'b1));  // open: RIN
  xor xor_1 (xor_1_out, Dout[7], Dout[5], Dout[4], Dout[3]);

  // Notes on the sheet:
  //   输入引脚
  //   请勿修改引脚名称、电路名称及电路封装外观
  //   输出引脚
endmodule
