// Logisim project lab4.4.circ as structural Verilog: 1 circuit, main circuit Shifter32
// 移位器
module Shifter32 (
  input  [4:0] shamt,
  input  L_R,
  input  A_L,
  input  [31:0] DataIn,
  output [31:0] DataOut
);

  wire not_1_out;
  wire [1:0] bit_extender_1_out, multiplexer_2_out_2, multiplexer_3_out;
  wire [3:0] bit_extender_2_out, multiplexer_5_out;
  wire [7:0] bit_extender_3_out, multiplexer_8_out;
  wire [15:0] bit_extender_4_out, multiplexer_9_out;
  wire [29:0] multiplexer_2_out;
  wire [31:0] multiplexer_4_out, multiplexer_6_out, multiplexer_7_out;
  wire [31:31] multiplexer_1_out;

  Multiplexer #(.enable("false")) multiplexer_1 (
    .in0(DataIn[31]), .in1(1'b0), .out(multiplexer_1_out[31]), .sel(not_1_out));
  not not_1 (not_1_out, A_L);
  assign bit_extender_1_out = {{1{multiplexer_1_out[31]}}, multiplexer_1_out[31]};  // Bit_Extender bit_extender_1
  Multiplexer #(.select(2), .width(32), .enable("false")) multiplexer_2 (
    .in0(DataIn), .in1({multiplexer_1_out[31], DataIn[31:1]}), .in2(DataIn),
    .in3({DataIn[30:0], multiplexer_1_out[31]}), .out({multiplexer_2_out, multiplexer_2_out_2}),
    .sel({L_R, shamt[0]}));
  Multiplexer #(.width(2), .enable("false")) multiplexer_3 (
    .in0(multiplexer_2_out[29:28]), .in1(2'b00), .out(multiplexer_3_out), .sel(not_1_out));
  assign bit_extender_2_out = {{2{bit_extender_1_out[1]}}, bit_extender_1_out};  // Bit_Extender bit_extender_2
  Multiplexer #(.select(2), .width(32), .enable("false")) multiplexer_4 (
    .in0({multiplexer_2_out, multiplexer_2_out_2}), .in1({bit_extender_1_out, multiplexer_2_out}),
    .in2({multiplexer_2_out, multiplexer_2_out_2}),
    .in3({multiplexer_2_out[27:0], multiplexer_2_out_2, multiplexer_3_out}), .out(multiplexer_4_out),
    .sel({L_R, shamt[1]}));
  Multiplexer #(.width(4), .enable("false")) multiplexer_5 (
    .in0(multiplexer_4_out[31:28]), .in1(4'b0000), .out(multiplexer_5_out), .sel(not_1_out));
  assign bit_extender_3_out = {{4{bit_extender_2_out[3]}}, bit_extender_2_out};  // Bit_Extender bit_extender_3
  Multiplexer #(.select(2), .width(32), .enable("false")) multiplexer_6 (
    .in0(multiplexer_4_out), .in1({bit_extender_2_out, multiplexer_4_out[31:4]}), .in2(multiplexer_4_out),
    .in3({multiplexer_4_out[27:0], multiplexer_5_out}), .out(multiplexer_6_out), .sel({L_R, shamt[2]}));
  assign bit_extender_4_out = {{8{bit_extender_3_out[7]}}, bit_extender_3_out};  // Bit_Extender bit_extender_4
  Multiplexer #(.select(2), .width(32), .enable("false")) multiplexer_7 (
    .in0(multiplexer_6_out), .in1({bit_extender_3_out, multiplexer_6_out[31:8]}), .in2(multiplexer_6_out),
    .in3({multiplexer_6_out[23:0], multiplexer_8_out}), .out(multiplexer_7_out), .sel({L_R, shamt[3]}));
  Multiplexer #(.width(8), .enable("false")) multiplexer_8 (
    .in0(multiplexer_6_out[31:24]), .in1({8{1'b0}}), .out(multiplexer_8_out), .sel(not_1_out));
  Multiplexer #(.width(16), .enable("false")) multiplexer_9 (
    .in0(multiplexer_7_out[31:16]), .in1({16{1'b0}}), .out(multiplexer_9_out), .sel(not_1_out));
  Multiplexer #(.select(2), .width(32), .enable("false")) multiplexer_10 (
    .in0(multiplexer_7_out), .in1({bit_extender_4_out, multiplexer_7_out[31:16]}), .in2(multiplexer_7_out),
    .in3({multiplexer_7_out[15:0], multiplexer_9_out}), .out(DataOut), .sel({L_R, shamt[4]}));

  // Other names for the same wires on the sheet: Din[31:0] = DataIn; Left_Right = L_R; Arth_Logic = A_L;
  //   Dout[31:0] = DataOut

  // Notes on the sheet:
  //   L/R,A/L: 00逻辑右移，01算术右移，10逻辑左移，11：循环左移
  //   输入引脚
  //   请勿修改引脚名称、电路名称及电路封装外观
  //   提示：使用多路选择器、逻辑门实现32位桶形移位器，禁止直接使用移位器组件。
  //   输出引脚
endmodule
