// Logisim project lab4.p1.circ as structural Verilog: 1 circuit, main circuit Adder32
// 加法器
module Adder32 (
  input  Cin,
  input  [31:0] X1,
  input  [31:0] X0,
  input  [31:0] Y1,
  input  [31:0] Y0,
  output CF,
  output Cout,
  output OF,
  output SF,
  output [31:0] S1,
  output ZF,
  output [31:0] S0
);

  wire adder16_1_gg, adder16_1_pg, adder16_2_gg, adder16_2_pg, adder16_3_gg, adder16_3_pg, adder16_4_gg,
       adder16_4_pg, and_2_out, and_3_out, clu4_1_c1, clu4_1_c2, clu4_1_c3, nor_1_out, nor_2_out;

  Adder16 adder16_1 (
    .X(X1[31:16]), .Y(Y1[31:16]), .C0(Cin), .S(S0[15:0]), .Pg(adder16_1_pg), .Gg(adder16_1_gg));  // open: C16
  Adder16 adder16_2 (
    .X(X1[15:0]), .Y(Y1[15:0]), .C0(clu4_1_c1), .S(S0[31:16]), .Pg(adder16_2_pg), .Gg(adder16_2_gg));  // open: C16
  Adder16 adder16_3 (
    .X(X0[31:16]), .Y(Y0[31:16]), .C0(clu4_1_c2), .S(S1[15:0]), .Pg(adder16_3_pg), .Gg(adder16_3_gg));  // open: C16
  Adder16 adder16_4 (
    .X(X0[15:0]), .Y(Y0[15:0]), .C0(clu4_1_c3), .S(S1[31:16]), .C16(Cout), .Pg(adder16_4_pg),
    .Gg(adder16_4_gg));
  CLU4 clu4_1 (
    .P0(adder16_1_pg), .P1(adder16_2_pg), .P2(adder16_3_pg), .P3(adder16_4_pg), .C1(clu4_1_c1),
    .C3(clu4_1_c3), .G0(adder16_1_gg), .G1(adder16_2_gg), .G2(adder16_3_gg), .G3(adder16_4_gg),
    .C2(clu4_1_c2), .C0(Cin));  // open: C4, Pg, Gg
  nor nor_1 (nor_1_out, S1[0], S1[1], S1[2], S1[3], S1[4], S1[5], S1[6], S1[7], S1[8], S1[9], S1[10], S1[11], S1[12], S1[13], S1[14], S1[15], S1[16], S1[17], S1[18], S1[19], S1[20], S1[21], S1[22], S1[23], S1[24], S1[25], S1[26], S1[27], S1[28], S1[29], S1[30], S1[31]);
  nor nor_2 (nor_2_out, S0[16], S0[17], S0[18], S0[19], S0[20], S0[21], S0[22], S0[23], S0[24], S0[25], S0[26], S0[27], S0[28], S0[29], S0[30], S0[31], S0[0], S0[1], S0[2], S0[3], S0[4], S0[5], S0[6], S0[7], S0[8], S0[9], S0[10], S0[11], S0[12], S0[13], S0[14], S0[15]);
  and and_1 (ZF, nor_1_out, nor_2_out);
  // Probe on X1
  // Probe on Y1
  // Probe on S1
  // Probe on X0
  // Probe on Y0
  // Probe on S0
  and and_2 (and_2_out, ~X1[31], ~Y1[31], S1[31]);  // AND_Gate
  or or_1 (OF, and_2_out, and_3_out);
  and and_3 (and_3_out, X1[31], Y1[31], ~S1[31]);  // AND_Gate
  xor xor_1 (CF, Cout, Cin);

  assign SF = S1[31];

  // Notes on the sheet:
  //   Cin: pull=down
  //   Y0: pull=down
  //   X1: pull=down
  //   X0: pull=down
  //   Y1: pull=down
  //   输入引脚区
  //   输出引脚区
  //   +
  //   =
  //   无符号加法
endmodule
