// Logisim project lab4.p2.circ as structural Verilog: 1 circuit, main circuit main
module main (
  input  [31:0] X,
  input  [31:0] Y,
  output [31:0] Z1,
  output [31:0] Z0
);

  wire adder_1_cout, adder_3_cout, adder_5_cout;
  wire [15:0] multiplier_1_cout, multiplier_1_out, multiplier_2_cout, multiplier_2_out, multiplier_3_cout,
       multiplier_3_out, multiplier_4_cout, multiplier_4_out;
  wire [31:0] adder_1_out, adder_2_out, adder_3_out, adder_4_out;

  Multiplier #(.width(16)) multiplier_1 (
    .a(X[15:0]), .b(Y[15:0]), .out(multiplier_1_out), .cout(multiplier_1_cout));  // open: cin
  Multiplier #(.width(16)) multiplier_2 (
    .a(X[15:0]), .b(Y[31:16]), .out(multiplier_2_out), .cout(multiplier_2_cout));  // open: cin
  Multiplier #(.width(16)) multiplier_3 (
    .a(X[31:16]), .b(Y[15:0]), .out(multiplier_3_out), .cout(multiplier_3_cout));  // open: cin
  Multiplier #(.width(16)) multiplier_4 (
    .a(X[31:16]), .b(Y[31:16]), .out(multiplier_4_out), .cout(multiplier_4_cout));  // open: cin
  Adder #(.width(32)) adder_1 (
    .a({multiplier_1_cout, multiplier_1_out}), .b({multiplier_2_out, {16{1'b0}}}), .out(adder_1_out),
    .cout(adder_1_cout));  // open: cin
  Adder #(.width(32)) adder_2 (
    .a({{16{1'b0}}, multiplier_2_cout}), .b({32{1'b0}}), .out(adder_2_out), .cin(adder_1_cout));  // open: cout
  Adder #(.width(32)) adder_3 (
    .a({32{1'b0}}), .b({multiplier_3_out, {16{1'b0}}}), .out(adder_3_out), .cout(adder_3_cout));  // open: cin
  Adder #(.width(32)) adder_4 (
    .a({{16{1'b0}}, multiplier_3_cout}), .b({multiplier_4_cout, multiplier_4_out}), .out(adder_4_out),
    .cin(adder_3_cout));  // open: cout
  Adder #(.width(32)) adder_5 (.a(adder_1_out), .b(adder_3_out), .out(Z0), .cout(adder_5_cout));  // open: cin
  Adder #(.width(32)) adder_6 (.a(adder_2_out), .b(adder_4_out), .out(Z1), .cin(adder_5_cout));  // open: cout
  // Probe on Z1
  // Probe on X
  // Probe on Y
  // Probe on Z0

  // Notes on the sheet:
  //   输入引脚
  //   输出引脚
  //   ×
  //   =
endmodule
