// Logisim project lab5.2.circ as structural Verilog: 2 circuits, main circuit DataRam
// DataRAM
module DataRam (
  input  CLK,
  input  CLR,
  input  WE,
  input  [2:0] MemOp,
  input  [17:0] Addr,
  input  [31:0] Din,
  output AlignErr,
  output [31:0] DataOut
);

  wire and_1_out, and_2_out, decoder_1_out0, decoder_1_out1, decoder_1_out2, decoder_1_out3, decoder_1_out4,
       decoder_1_out5, decoder_1_out6, decoder_1_out7, decoder_2_out0, decoder_2_out1, decoder_2_out2,
       decoder_2_out3, SEL0, SEL1, SEL2, SEL3, xor_1_out_4, xor_2_out_4, xor_3_out_4, xor_4_out_4,
       xor_5_out_4, xor_6_out_4;
  wire [7:0] Byte;
  wire [15:0] Half;
  wire [31:0] bit_extender_1_out, bit_extender_2_out, bit_extender_3_out, bit_extender_4_out,
       multiplexer_1_out, Word;

  Decoder #(.select(3), .enable("false")) decoder_1 (
    .out0(decoder_1_out0), .out1(decoder_1_out1), .out2(decoder_1_out2), .out3(decoder_1_out3),
    .out4(decoder_1_out4), .out5(decoder_1_out5), .out6(decoder_1_out6), .out7(decoder_1_out7), .sel(MemOp));
  Decoder #(.select(2), .enable("false")) decoder_2 (
    .out0(decoder_2_out0), .out1(decoder_2_out1), .out2(decoder_2_out2), .out3(decoder_2_out3),
    .sel(Addr[1:0]));
  nor nor_1 (AlignErr, SEL3, SEL2, SEL1, SEL0);
  and and_1 (and_1_out, decoder_2_out0, decoder_1_out0);
  \xor  xor_1 (.out_4(xor_1_out_4), .in_1(decoder_2_out3), .in_2(decoder_1_out1), .in_3(decoder_1_out5));
  or or_1 (SEL3, xor_1_out_4, and_1_out, xor_2_out_4);
  Multiplexer #(.select(2), .width(32), .enable("false")) multiplexer_1 (
    .in0(Din), .in1({Din[7:0], Din[7:0], Din[7:0], Din[7:0]}), .in2({Din[15:0], Din[15:0]}),
    .out(multiplexer_1_out), .sel(MemOp[1:0]));  // open: in3
  \xor  xor_2 (.out_4(xor_2_out_4), .in_1(decoder_2_out2), .in_2(decoder_1_out2), .in_3(decoder_1_out6));
  \xor  xor_3 (.out_4(xor_3_out_4), .in_1(decoder_2_out2), .in_2(decoder_1_out1), .in_3(decoder_1_out5));
  or or_2 (SEL2, xor_3_out_4, and_1_out, xor_2_out_4);
  Multiplexer #(.width(16), .enable("false")) multiplexer_2 (
    .in0(Word[15:0]), .in1(Word[31:16]), .out(Half), .sel(Addr[1]));
  \xor  xor_4 (.out_4(xor_4_out_4), .in_1(decoder_2_out1), .in_2(decoder_1_out1), .in_3(decoder_1_out5));
  or or_3 (SEL1, xor_4_out_4, and_2_out, xor_6_out_4);
  RAM #(.addrWidth(16), .bus("separate"), .Select("high")) ram_1 (
    .addr(Addr[17:2]), .din(multiplexer_1_out[7:0]), .data(Word[7:0]), .str(WE), .sel(SEL0), .clk(CLK),
    .clr(CLR));  // open: ld
  Multiplexer #(.select(2), .width(8), .enable("false")) multiplexer_3 (
    .in0(Word[7:0]), .in1(Word[15:8]), .in2(Word[23:16]), .in3(Word[31:24]), .out(Byte), .sel(Addr[1:0]));
  \xor  xor_5 (.out_4(xor_5_out_4), .in_1(decoder_2_out0), .in_2(decoder_1_out1), .in_3(decoder_1_out5));
  \xor  xor_6 (.out_4(xor_6_out_4), .in_1(decoder_2_out0), .in_2(decoder_1_out2), .in_3(decoder_1_out6));
  and and_2 (and_2_out, decoder_2_out0, decoder_1_out0);
  or or_4 (SEL0, xor_5_out_4, and_2_out, xor_6_out_4);
  RAM #(.addrWidth(16), .bus("separate"), .Select("high")) ram_2 (
    .addr(Addr[17:2]), .din(multiplexer_1_out[15:8]), .data(Word[15:8]), .str(WE), .sel(SEL1), .clk(CLK),
    .clr(CLR));  // open: ld
  assign bit_extender_1_out = {{24{1'b0}}, Byte};  // Bit_Extender bit_extender_1
  assign bit_extender_2_out = {{16{1'b0}}, Half};  // Bit_Extender bit_extender_2
  assign bit_extender_3_out = {{24{Byte[7]}}, Byte};  // Bit_Extender bit_extender_3
  assign bit_extender_4_out = {{16{Half[15]}}, Half};  // Bit_Extender bit_extender_4
  RAM #(.addrWidth(16), .bus("separate"), .Select("high")) ram_3 (
    .addr(Addr[17:2]), .din(multiplexer_1_out[23:16]), .data(Word[23:16]), .str(WE), .sel(SEL2), .clk(CLK),
    .clr(CLR));  // open: ld
  Multiplexer #(.select(3), .width(32), .enable("false")) multiplexer_4 (
    .in0(Word), .in1(bit_extender_1_out), .in2(bit_extender_2_out), .in5(bit_extender_3_out),
    .in6(bit_extender_4_out), .out(DataOut), .sel(MemOp));  // open: in3, in4, in7
  RAM #(.addrWidth(16), .bus("separate"), .Select("high")) ram_4 (
    .addr(Addr[17:2]), .din(multiplexer_1_out[31:24]), .data(Word[31:24]), .str(WE), .sel(SEL3), .clk(CLK),
    .clr(CLR));  // open: ld

  // Other names for the same wires on the sheet: Dout[31:0] = DataOut

  // Notes on the sheet:
  //   输入引脚
  //   请勿修改引脚名称、电路名称及电路封装外观
  //   为了后续实验中的引用，不要修改MemOp的编码定义、引脚名称和在布局中的位置。
  //   32位数据存储器，按字节分4片存储，可按照字节、半字和字进行存储；读取字节或半字时，支持0扩展和符号位扩展。
  //   输出引脚
endmodule

module \xor  (
  input  in_1,
  input  in_2,
  input  in_3,
  output out_4
);

  wire and_1_out, and_2_out, and_3_out;

  and and_1 (and_1_out, ~in_1, in_2, in_3);  // AND_Gate
  or or_1 (out_4, and_1_out, and_2_out, and_3_out);
  and and_2 (and_2_out, in_1, ~in_2, in_3);  // AND_Gate
  and and_3 (and_3_out, in_1, in_2, ~in_3);  // AND_Gate
endmodule
