// Logisim project lab5.5.circ as structural Verilog: 16 circuits, main circuit main
module main (
  input  [2:0] ExtOp,
  input  [2:0] MemOp,
  input  RegWr,
  input  ALUASrc,
  input  MemWr,
  input  [1:0] ALUBSrc,
  input  [31:0] Initial_Address,
  input  [3:0] ALUctr,
  input  MemtoReg,
  input  [2:0] BandJ,
  input  clk,
  input  ReSet,
  output [31:0] PC,
  output [31:0] BusW,
  output [31:0] Din,
  output NPCASrc,
  output NPCBSrc
);


  // Other names for the same wires on the sheet: Init_Addr[31:0] = Initial_Address

  // Notes on the sheet:
  //   NPCASrc: pull=down
  //   RegWr: pull=down
  //   BandJ: pull=down
  //   ALUASrc: pull=down
  //   ALUBSrc: pull=down
  //   NPCBSrc: pull=down
  //   ExtOp: pull=down
  //   ALUctr: pull=down
  //   输入信号
  //   请勿修改引脚名称、电路名称及电路封装外观
  //   为了后续实验中的引用，不要修改控制信号的编码定义、引脚名称和在布局中的位置。
  //   指令存储器和数据存储器数据位都是32位，指令存储器编址以字为单位，数据存储器编址以字节为单位。
  //   32位数据存储器，按字节分4片存储，可按照字节、半字和字进行存储；读取字节或半字时，支持0扩展和符号位扩展。
  //   输出信号
endmodule

module BandJ (
  input  [2:0] Branch,
  input  Zero,
  input  Result0,
  output NxtASrc,
  output NxtBSrc
);


  // Notes on the sheet:
  //   Zero: pull=down
  //   Branch: pull=down
  //   输入信号
  //   请勿修改引脚名称、电路名称及电路封装外观
  //   不要修改控制信号的编码定义、引脚名称和在布局中的位置。
  //   输出信号
endmodule

module IFU (
  input  [31:0] Initial_Address,
  input  [31:0] Imm,
  input  [31:0] BusA,
  input  CLK,
  input  Reset,
  input  NxtASrc,
  input  NxtBSrc,
  output [31:0] PC
);

  wire NPCASrc, NPCBSrc;
  wire [31:0] adder_1_out, IR, multiplexer_1_out, multiplexer_2_out, multiplexer_3_out;

  Multiplexer #(.width(32), .enable("false")) multiplexer_1 (
    .in0(PC), .in1(BusA), .out(multiplexer_1_out), .sel(NPCASrc));
  Multiplexer #(.width(32), .enable("false")) multiplexer_2 (
    .in0(32'h4), .in1(Imm), .out(multiplexer_2_out), .sel(NPCBSrc));
  Adder #(.width(32)) adder_1 (.a(multiplexer_1_out), .b(multiplexer_2_out), .out(adder_1_out));  // open: cin, cout
  Multiplexer #(.width(32), .enable("false")) multiplexer_3 (
    .in0(adder_1_out), .in1(Initial_Address), .out(multiplexer_3_out), .sel(Reset));
  Register #(.width(32), .Select("low")) register_1 (.D(multiplexer_3_out), .Q(PC), .clk(CLK));  // open: en, clr
  ROM #(.addrWidth(16), .dataWidth(32), .Select("low")) rom_1 (.addr(PC[17:2]), .data(IR));

  // Other names for the same wires on the sheet: Init_Addr[31:0] = Initial_Address

  // Notes on the sheet:
  //   Imm: pull=down
  //   NxtBSrc: pull=down
  //   BusA: pull=down
  //   NxtASrc: pull=down
  //   输入信号
  //   请勿修改引脚名称、电路名称及电路封装外观
  //   指令存储器256KB，数据位为32位，地址位为16位。PC寄存器数据宽度32位，片选信号高电平有效
  //   输出信号
  //   contents of rom_1 (hex, n*v repeats v):
  //   256*0 2083 8133 106213 406293 fff06313 4410663 106193 406393 806413 21b5b3 2058063 3a483 42503
  //   a4b5b3 458c63 a3a023 942023 c0006f 610133 fc9ff06f 4181b3 5383b3 540433 fc9ff06f 6f 0 0 413 9117
  //   ffc10113 94000ef 50463 8067 ff010113 100513 112623 74000ef ff010113 812423 912223 15c00413 1212023
  //   112623 c400493 9840913 442783 42703 4a503 440413 e787b3 40f50533 153513 f42223 448493 fa5ff0ef
  //   fd241ce3 100513 f99ff0ef c12083 812403 412483 12903 513 1010113 8067 1ea02e23 6f ff010113 b800513
  //   112623 f7dff0ef 1ea02e23 6f 0 1 1 2 3 5 8 d 15 22 37 59 90 e9 179 262 3db 63d a18 1055 1a6d 2ac2
  //   452f 6ff1 b520 12511 1da31 2ff42 4d973 7d8b5 cb228 148add 213d05 35c7e2 5704e7 8cccc9 e3d1b0 1709e79
  //   2547029 3c50ea2 6197ecb 1 1 deadbeef 395*0 413 9117 ffc10113 ec000ef 50463 8067 ff010113 100513
  //   112623 cc000ef ff010113 19400813 112623 812423 912223 1212023 100793 f82223 f82023 880593 7c80313
  //   100713 19800513 100893 50493 50793 100693 80006f 7a703 d70633 c7a023 478793 70693 feb796e3 117a023
  //   478593 658663 482703 fc9ff06f 11400413 7c40913 100793 c0006f 4a783 448493 42503 440413 40f50533
  //   153513 f4dff0ef fe8912e3 100513 f41ff0ef c12083 812403 412483 12903 513 1010113 8067 18a02823 6f
  //   ff010113 11000513 112623 f25ff0ef 18a02823 6f 0 1 1e 1b3 fdc 6b0d 22caa 90f6f 1f1058 594efd da4f4e
  //   1ca7357 3418be4 527c829 72363ea 8aaf953 93ee7d0 8aaf953 72363ea 527c829 3418be4 1ca7357 da4f4e
  //   594efd 1f1058 90f6f 22caa 6b0d fdc 1b3 1e 1 2 3 4 5 6 7 8 9 a b c d e f 10 11 12 13 14 15 16 17 18
  //   19 1a 1b 1c 1d 1e 1f deadbeef deadbeef 444*0 413 9117 ffc10113 39c000ef 50463 8067 ff010113 100513
  //   112623 380000ef 259693 d506b3 50893 6a803 60513 6c5dc63 261793 f887b3 7a783 fff50613 261613 c88633
  //   140006f fff50513 472783 6b50863 70613 ffc60713 fef846e3 259693 d886b3 251313 f6a023 688633 4a5de63
  //   68713 c0006f 158593 2a58463 72783 70693 470713 fef856e3 f62023 f8a5cee3 58513 106a023 8067 6886b3
  //   6a783 f62023 106a023 8067 251693 d886b3 f6a023 fe9ff06f 58513 fe1ff06f 1ec5da63 fa010113 4812c23
  //   5612023 3812c23 4112e23 4912a23 5212823 5312623 5412423 5512223 3712e23 3912a23 3a12823 3b12623
  //   58c13 60b13 50413 b0613 c0593 40513 ee9ff0ef a12223 fff50c93 159c5663 c8613 c0593 40513 ecdff0ef
  //   a12423 fff50d13 13ac5263 d0613 c0593 40513 eb1ff0ef a12623 fff50d93 fbc5e63 d8613 c0593 40513
  //   e95ff0ef a12823 fff50993 d3c5a63 98613 c0593 40513 e79ff0ef fff50913 50493 b2c5863 90613 c0593 40513
  //   e5dff0ef fff50b93 50a13 97c5663 b8613 c0593 40513 e41ff0ef a12a23 fff50a93 75c5263 a8613 c0593 40513
  //   e25ff0ef fff50693 50713 4dc5063 68613 c0593 40513 e12e23 d12c23 e01ff0ef 50813 c0593 fff50613 40513
  //   180c13 eadff0ef 1812683 1c12703 fcdc44e3 170c13 fb5c42e3 1412783 178c13 f77c4ee3 1a0c13 f52c4ce3
  //   148c13 f33c4ae3 1012783 178c13 f1bc46e3 c12783 178c13 efac42e3 812783 178c13 eb9c4ee3 412783 178c13
  //   e96c4ae3 5c12083 5812403 5412483 5012903 4c12983 4812a03 4412a83 4012b03 3c12b83 3812c03 3412c83
  //   3012d03 2c12d83 6010113 8067 8067 fe010113 1412423 1300613 593 3c000513 812c23 912a23 1212823
  //   1312623 112e23 3c000493 dddff0ef 3c000913 413 1400993 92503 490913 40850533 153513 140413 cddff0ef
  //   ff3414e3 100513 cd1ff0ef 1300613 593 3c000513 d9dff0ef 413 1400913 4a503 448493 40850533 153513
  //   140413 ca1ff0ef ff2414e3 100513 c95ff0ef 1c12083 1812403 1412483 1012903 c12983 812a03 513 2010113
  //   8067 6f ff010113 3bc00513 112623 f31ff0ef 6f 0 2 c e 6 d f 10 a 0 12 b 13 9 1 7 5 4 3 8 11 deadbeef
  //   deadbeef 63658*0 413 9117 ffc10113 39c000ef 50463 8067 ff010113 100513 112623 380000ef 259693 d506b3
  //   50893 6a803 60513 6c5dc63 261793 f887b3 7a783 fff50613 261613 c88633 140006f fff50513 472783 6b50863
  //   70613 ffc60713 fef846e3 259693 d886b3 251313 f6a023 688633 4a5de63 68713 c0006f 158593 2a58463 72783
  //   70693 470713 fef856e3 f62023 f8a5cee3 58513 106a023 8067 6886b3 6a783 f62023 106a023 8067 251693
  //   d886b3 f6a023 fe9ff06f 58513 fe1ff06f 1ec5da63 fa010113 4812c23 5612023 3812c23 4112e23 4912a23
  //   5212823 5312623 5412423 5512223 3712e23 3912a23 3a12823 3b12623 58c13 60b13 50413 b0613 c0593 40513
  //   ee9ff0ef a12223 fff50c93 159c5663 c8613 c0593 40513 ecdff0ef a12423 fff50d13 13a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
endmodule

module IDU (
  input  [31:0] IR,
  input  [31:0] BusW,
  input  [31:0] PC,
  input  [2:0] ExtOp,
  input  RegWr,
  input  ALUASrc,
  input  [1:0] ALUBSrc,
  input  CLK,
  output [31:0] DataA,
  output [31:0] DataB,
  output [31:0] BusA,
  output [31:0] BusB,
  output [6:0] OpCode,
  output [31:0] Imm,
  output [2:0] Funct3,
  output [6:0] Funct7
);

  \立即数扩展器  \u_立即数扩展器_1  (.Instr(IR), .Extop(ExtOp), .imm(Imm));
  RegFile regfile_1 (
    .R1_num(IR[19:15]), .R2_num(IR[24:20]), .Write_Reg_num(IR[11:7]), .Write_Enable(RegWr), .Clock(CLK),
    .Din(BusW), .Reg1Out(BusA), .Reg2Out(BusB));
  Multiplexer #(.width(32), .enable("false")) multiplexer_1 (.in0(BusA), .in1(PC), .out(DataA), .sel(ALUASrc));
  Multiplexer #(.select(2), .width(32), .enable("false")) multiplexer_2 (
    .in0(BusB), .in1(32'h4), .in2(Imm), .out(DataB), .sel(ALUBSrc));  // open: in3

  assign Funct3 = IR[14:12];
  assign Funct7 = IR[31:25];
  assign OpCode = IR[6:0];

  // Other names for the same wires on the sheet: op[6:0] = IR[6:0]

  // Notes on the sheet:
  //   BusW: pull=down
  //   ALUASrc: pull=down
  //   ALUBSrc: pull=down
  //   PC: pull=down
  //   ExtOp: pull=down
  //   RegWr: pull=down
  //   输入信号
  //   为了后续实验中的引用，不要修改ALUASrc、ALUBSrc和EXtOP编码定义。
  //   请勿修改引脚名称、电路名称及电路封装外观
  //   输出信号
  //   修改寄存器堆电路设计，0号寄存器始终为0。
endmodule

module RegFile (
  input  [4:0] R1_num,
  input  [4:0] R2_num,
  input  [4:0] Write_Reg_num,
  input  [31:0] Din,
  input  Write_Enable,
  input  Clock,
  output [31:0] Reg1Out,
  output [31:0] Reg2Out
);

  wire decoder_1_out1, decoder_1_out2, decoder_1_out3, decoder_1_out4, decoder_1_out5, decoder_1_out6,
       decoder_1_out7, decoder_1_out8, decoder_1_out9, decoder_1_out10, decoder_1_out11, decoder_1_out12,
       decoder_1_out13, decoder_1_out14, decoder_1_out15, decoder_1_out16, decoder_1_out17, decoder_1_out18,
       decoder_1_out19, decoder_1_out20, decoder_1_out21, decoder_1_out22, decoder_1_out23, decoder_1_out24,
       decoder_1_out25, decoder_1_out26, decoder_1_out27, decoder_1_out28, decoder_1_out29, decoder_1_out30,
       decoder_1_out31;
  wire [31:0] _1_q, _2_q, _3_q, _4_q, _5_q, _6_q, _7_q, _8_q, _9_q, register_1_q, register_2_q, register_3_q,
       register_4_q, register_5_q, register_6_q, register_7_q, register_8_q, register_9_q, register_10_q,
       register_11_q, register_12_q, register_13_q, register_14_q, register_15_q, register_16_q,
       register_17_q, register_18_q, register_19_q, register_20_q, register_21_q, register_22_q;

  Decoder #(.select(5), .disabled(0)) decoder_1 (
    .out1(decoder_1_out1), .out2(decoder_1_out2), .out3(decoder_1_out3), .out4(decoder_1_out4),
    .out5(decoder_1_out5), .out6(decoder_1_out6), .out7(decoder_1_out7), .out8(decoder_1_out8),
    .out9(decoder_1_out9), .out10(decoder_1_out10), .out11(decoder_1_out11), .out12(decoder_1_out12),
    .out13(decoder_1_out13), .out14(decoder_1_out14), .out15(decoder_1_out15), .out16(decoder_1_out16),
    .out17(decoder_1_out17), .out18(decoder_1_out18), .out19(decoder_1_out19), .out20(decoder_1_out20),
    .out21(decoder_1_out21), .out22(decoder_1_out22), .out23(decoder_1_out23), .out24(decoder_1_out24),
    .out25(decoder_1_out25), .out26(decoder_1_out26), .out27(decoder_1_out27), .out28(decoder_1_out28),
    .out29(decoder_1_out29), .out30(decoder_1_out30), .out31(decoder_1_out31), .sel(Write_Reg_num),
    .en(Write_Enable));  // open: out0
  Register #(.width(32), .Select("low")) _1 (.D(Din), .en(decoder_1_out1), .Q(_1_q), .clk(Clock));  // open: clr
  Register #(.width(32), .Select("low")) _2 (.D(Din), .en(decoder_1_out2), .Q(_2_q), .clk(Clock));  // open: clr
  Register #(.width(32), .Select("low")) _3 (.D(Din), .en(decoder_1_out3), .Q(_3_q), .clk(Clock));  // open: clr
  Register #(.width(32), .Select("low")) _4 (.D(Din), .en(decoder_1_out4), .Q(_4_q), .clk(Clock));  // open: clr
  Register #(.width(32), .Select("low")) _5 (.D(Din), .en(decoder_1_out5), .Q(_5_q), .clk(Clock));  // open: clr
  Register #(.width(32), .Select("low")) _6 (.D(Din), .en(decoder_1_out6), .Q(_6_q), .clk(Clock));  // open: clr
  Register #(.width(32), .Select("low")) _7 (.D(Din), .en(decoder_1_out7), .Q(_7_q), .clk(Clock));  // open: clr
  Register #(.width(32), .Select("low")) _8 (.D(Din), .en(decoder_1_out8), .Q(_8_q), .clk(Clock));  // open: clr
  Register #(.width(32), .Select("low")) _9 (.D(Din), .en(decoder_1_out9), .Q(_9_q), .clk(Clock));  // open: clr
  Register #(.width(32), .Select("low")) register_1 (
    .D(Din), .en(decoder_1_out10), .Q(register_1_q), .clk(Clock));  // open: clr
  Register #(.width(32), .Select("low")) register_2 (
    .D(Din), .en(decoder_1_out11), .Q(register_2_q), .clk(Clock));  // open: clr
  Register #(.width(32), .Select("low")) register_3 (
    .D(Din), .en(decoder_1_out12), .Q(register_3_q), .clk(Clock));  // open: clr
  Register #(.width(32), .Select("low")) register_4 (
    .D(Din), .en(decoder_1_out13), .Q(register_4_q), .clk(Clock));  // open: clr
  Register #(.width(32), .Select("low")) register_5 (
    .D(Din), .en(decoder_1_out14), .Q(register_5_q), .clk(Clock));  // open: clr
  Register #(.width(32), .Select("low")) register_6 (
    .D(Din), .en(decoder_1_out15), .Q(register_6_q), .clk(Clock));  // open: clr
  Register #(.width(32), .Select("low")) register_7 (
    .D(Din), .en(decoder_1_out16), .Q(register_7_q), .clk(Clock));  // open: clr
  Register #(.width(32), .Select("low")) register_8 (
    .D(Din), .en(decoder_1_out17), .Q(register_8_q), .clk(Clock));  // open: clr
  Register #(.width(32), .Select("low")) register_9 (
    .D(Din), .en(decoder_1_out18), .Q(register_9_q), .clk(Clock));  // open: clr
  Register #(.width(32), .Select("low")) register_10 (
    .D(Din), .en(decoder_1_out19), .Q(register_10_q), .clk(Clock));  // open: clr
  Register #(.width(32), .Select("low")) register_11 (
    .D(Din), .en(decoder_1_out20), .Q(register_11_q), .clk(Clock));  // open: clr
  Register #(.width(32), .Select("low")) register_12 (
    .D(Din), .en(decoder_1_out21), .Q(register_12_q), .clk(Clock));  // open: clr
  Register #(.width(32), .Select("low")) register_13 (
    .D(Din), .en(decoder_1_out22), .Q(register_13_q), .clk(Clock));  // open: clr
  Register #(.width(32), .Select("low")) register_14 (
    .D(Din), .en(decoder_1_out23), .Q(register_14_q), .clk(Clock));  // open: clr
  Register #(.width(32), .Select("low")) register_15 (
    .D(Din), .en(decoder_1_out24), .Q(register_15_q), .clk(Clock));  // open: clr
  Register #(.width(32), .Select("low")) register_16 (
    .D(Din), .en(decoder_1_out25), .Q(register_16_q), .clk(Clock));  // open: clr
  Register #(.width(32), .Select("low")) register_17 (
    .D(Din), .en(decoder_1_out26), .Q(register_17_q), .clk(Clock));  // open: clr
  Register #(.width(32), .Select("low")) register_18 (
    .D(Din), .en(decoder_1_out27), .Q(register_18_q), .clk(Clock));  // open: clr
  Register #(.width(32), .Select("low")) register_19 (
    .D(Din), .en(decoder_1_out28), .Q(register_19_q), .clk(Clock));  // open: clr
  Register #(.width(32), .Select("low")) register_20 (
    .D(Din), .en(decoder_1_out29), .Q(register_20_q), .clk(Clock));  // open: clr
  Register #(.width(32), .Select("low")) register_21 (
    .D(Din), .en(decoder_1_out30), .Q(register_21_q), .clk(Clock));  // open: clr
  Register #(.width(32), .Select("low")) register_22 (
    .D(Din), .en(decoder_1_out31), .Q(register_22_q), .clk(Clock));  // open: clr
  Multiplexer #(.select(5), .width(32), .enable("false")) multiplexer_1 (
    .in0({32{1'b0}}), .in1(_1_q), .in2(_2_q), .in3(_3_q), .in4(_4_q), .in5(_5_q), .in6(_6_q), .in7(_7_q),
    .in8(_8_q), .in9(_9_q), .in10(register_1_q), .in11(register_2_q), .in12(register_3_q),
    .in13(register_4_q), .in14(register_5_q), .in15(register_6_q), .in16(register_7_q), .in17(register_8_q),
    .in18(register_9_q), .in19(register_10_q), .in20(register_11_q), .in21(register_12_q),
    .in22(register_13_q), .in23(register_14_q), .in24(register_15_q), .in25(register_16_q),
    .in26(register_17_q), .in27(register_18_q), .in28(register_19_q), .in29(register_20_q),
    .in30(register_21_q), .in31(register_22_q), .out(Reg1Out), .sel(R1_num));
  Multiplexer #(.select(5), .width(32), .enable("false")) multiplexer_2 (
    .in0({32{1'b0}}), .in1(_1_q), .in2(_2_q), .in3(_3_q), .in4(_4_q), .in5(_5_q), .in6(_6_q), .in7(_7_q),
    .in8(_8_q), .in9(_9_q), .in10(register_1_q), .in11(register_2_q), .in12(register_3_q),
    .in13(register_4_q), .in14(register_5_q), .in15(register_6_q), .in16(register_7_q), .in17(register_8_q),
    .in18(register_9_q), .in19(register_10_q), .in20(register_11_q), .in21(register_12_q),
    .in22(register_13_q), .in23(register_14_q), .in24(register_15_q), .in25(register_16_q),
    .in26(register_17_q), .in27(register_18_q), .in28(register_19_q), .in29(register_20_q),
    .in30(register_21_q), .in31(register_22_q), .out(Reg2Out), .sel(R2_num));

  // Other names for the same wires on the sheet: CLK = Clock; RA[4:0] = R1_num; RB[4:0] = R2_num; RDA[31:0] = Reg1Out;
  //   RDB[31:0] = Reg2Out; RW[4:0] = Write_Reg_num; WE = Write_Enable

  // Notes on the sheet:
  //   输入引脚
  //   请勿修改引脚名称、电路名称及电路封装外观
  //   提示：使用译码器、多路选择器和32位寄存器及逻辑门实现寄存器堆，禁止直接使用存储器组件。
  //   输出引脚
endmodule

module \立即数扩展器  (
  input  [31:0] Instr,
  input  [2:0] Extop,
  output [31:0] imm
);

  wire [11:0] bit_extender_4_out;
  wire [19:0] bit_extender_3_out;
  wire [26:0] bit_extender_2_out;
  wire [31:0] bit_extender_1_out;

  assign bit_extender_1_out = {{20{Instr[31]}}, Instr[31:20]};  // Bit_Extender bit_extender_1
  assign bit_extender_2_out = {{20{Instr[31]}}, Instr[31:25]};  // Bit_Extender bit_extender_2
  assign bit_extender_3_out = {{19{Instr[31]}}, Instr[31]};  // Bit_Extender bit_extender_3
  assign bit_extender_4_out = {{11{Instr[31]}}, Instr[31]};  // Bit_Extender bit_extender_4
  Multiplexer #(.select(3), .width(32), .enable("false")) multiplexer_1 (
    .in0(bit_extender_1_out), .in1({Instr[31:12], {12{1'b0}}}), .in2({bit_extender_2_out, Instr[11:7]}),
    .in3({bit_extender_3_out, Instr[7], Instr[30:25], Instr[11:8], 1'b0}),
    .in4({bit_extender_4_out, Instr[19:12], Instr[20], Instr[30:21], 1'b0}), .out(imm), .sel(Extop));  // open: in5, in6, in7

  // Notes on the sheet:
  //   Instr: pull=down
  //   Extop: pull=down
  //   输入引脚
  //   输出引脚
endmodule

module DataRAM (
  input  CLK,
  input  CLR,
  input  WE,
  input  [2:0] MemOp,
  input  [17:0] Addr,
  input  [31:0] Din,
  output AlignErr,
  output [31:0] DataOut
);

  wire and_1_out, and_2_out, decoder_1_out0, decoder_1_out1, decoder_1_out2, decoder_1_out3, decoder_1_out4,
       decoder_1_out5, decoder_1_out6, decoder_1_out7, decoder_2_out0, decoder_2_out1, decoder_2_out2,
       decoder_2_out3, SEL0, SEL1, SEL2, SEL3, xor_1_out_4, xor_2_out_4, xor_3_out_4, xor_4_out_4,
       xor_5_out_4, xor_6_out_4;
  wire [7:0] Byte;
  wire [15:0] Half;
  wire [31:0] bit_extender_1_out, bit_extender_2_out, bit_extender_3_out, bit_extender_4_out,
       multiplexer_1_out, Word;

  Decoder #(.select(3), .enable("false")) decoder_1 (
    .out0(decoder_1_out0), .out1(decoder_1_out1), .out2(decoder_1_out2), .out3(decoder_1_out3),
    .out4(decoder_1_out4), .out5(decoder_1_out5), .out6(decoder_1_out6), .out7(decoder_1_out7), .sel(MemOp));
  Decoder #(.select(2), .enable("false")) decoder_2 (
    .out0(decoder_2_out0), .out1(decoder_2_out1), .out2(decoder_2_out2), .out3(decoder_2_out3),
    .sel(Addr[1:0]));
  nor nor_1 (AlignErr, SEL3, SEL2, SEL1, SEL0);
  \xor  xor_1 (.out_4(xor_1_out_4), .in_1(decoder_2_out3), .in_2(decoder_1_out1), .in_3(decoder_1_out5));
  and and_1 (and_1_out, decoder_2_out0, decoder_1_out0);
  or or_1 (SEL3, xor_1_out_4, and_1_out, xor_2_out_4);
  Multiplexer #(.select(2), .width(32), .enable("false")) multiplexer_1 (
    .in0(Din), .in1({Din[7:0], Din[7:0], Din[7:0], Din[7:0]}), .in2({Din[15:0], Din[15:0]}),
    .out(multiplexer_1_out), .sel(MemOp[1:0]));  // open: in3
  \xor  xor_2 (.out_4(xor_2_out_4), .in_1(decoder_2_out2), .in_2(decoder_1_out2), .in_3(decoder_1_out6));
  \xor  xor_3 (.out_4(xor_3_out_4), .in_1(decoder_2_out2), .in_2(decoder_1_out1), .in_3(decoder_1_out5));
  or or_2 (SEL2, xor_3_out_4, and_1_out, xor_2_out_4);
  Multiplexer #(.width(16), .enable("false")) multiplexer_2 (
    .in0(Word[15:0]), .in1(Word[31:16]), .out(Half), .sel(Addr[1]));
  \xor  xor_4 (.out_4(xor_4_out_4), .in_1(decoder_2_out1), .in_2(decoder_1_out1), .in_3(decoder_1_out5));
  or or_3 (SEL1, xor_4_out_4, and_2_out, xor_5_out_4);
  RAM #(.addrWidth(16), .bus("separate"), .Select("high")) ram_1 (
    .addr(Addr[17:2]), .din(multiplexer_1_out[7:0]), .data(Word[7:0]), .str(WE), .sel(SEL0), .clk(CLK),
    .clr(CLR));  // open: ld
  Multiplexer #(.select(2), .width(8), .enable("false")) multiplexer_3 (
    .in0(Word[7:0]), .in1(Word[15:8]), .in2(Word[23:16]), .in3(Word[31:24]), .out(Byte), .sel(Addr[1:0]));
  \xor  xor_5 (.out_4(xor_5_out_4), .in_1(decoder_2_out0), .in_2(decoder_1_out2), .in_3(decoder_1_out6));
  \xor  xor_6 (.out_4(xor_6_out_4), .in_1(decoder_2_out0), .in_2(decoder_1_out1), .in_3(decoder_1_out5));
  and and_2 (and_2_out, decoder_2_out0, decoder_1_out0);
  or or_4 (SEL0, xor_6_out_4, and_2_out, xor_5_out_4);
  RAM #(.addrWidth(16), .bus("separate"), .Select("high")) ram_2 (
    .addr(Addr[17:2]), .din(multiplexer_1_out[15:8]), .data(Word[15:8]), .str(WE), .sel(SEL1), .clk(CLK),
    .clr(CLR));  // open: ld
  assign bit_extender_1_out = {{24{1'b0}}, Byte};  // Bit_Extender bit_extender_1
  assign bit_extender_2_out = {{16{1'b0}}, Half};  // Bit_Extender bit_extender_2
  assign bit_extender_3_out = {{24{Byte[7]}}, Byte};  // Bit_Extender bit_extender_3
  assign bit_extender_4_out = {{16{Half[15]}}, Half};  // Bit_Extender bit_extender_4
  RAM #(.addrWidth(16), .bus("separate"), .Select("high")) ram_3 (
    .addr(Addr[17:2]), .din(multiplexer_1_out[23:16]), .data(Word[23:16]), .str(WE), .sel(SEL2), .clk(CLK),
    .clr(CLR));  // open: ld
  Multiplexer #(.select(3), .width(32), .enable("false")) multiplexer_4 (
    .in0(Word), .in1(bit_extender_1_out), .in2(bit_extender_2_out), .in5(bit_extender_3_out),
    .in6(bit_extender_4_out), .out(DataOut), .sel(MemOp));  // open: in3, in4, in7
  RAM #(.addrWidth(16), .bus("separate"), .Select("high")) ram_4 (
    .addr(Addr[17:2]), .din(multiplexer_1_out[31:24]), .data(Word[31:24]), .str(WE), .sel(SEL3), .clk(CLK),
    .clr(CLR));  // open: ld

  // Other names for the same wires on the sheet: Dout[31:0] = DataOut

  // Notes on the sheet:
  //   输入引脚
  //   请勿修改引脚名称、电路名称及电路封装外观
  //   为了后续实验中的引用，不要修改MemOp的编码定义、引脚名称和在布局中的位置。
  //   32位数据存储器，按字节分4片存储，可按照字节、半字和字进行存储；读取字节或半字时，支持0扩展和符号位扩展。
  //   输出引脚
endmodule

module ALU (
  input  [3:0] ALUctr,
  input  [31:0] A,
  input  [31:0] B,
  output Zero,
  output [31:0] S
);

  // Probe on A
  // Probe on B
  // Probe on S

  // Other names for the same wires on the sheet: Result[31:0] = S

  // Notes on the sheet:
  //   ALUctr: pull=down
  //   A: pull=down
  //   B: pull=down
  //   输入引脚
  //   请勿修改引脚名称、电路名称及电路封装外观
  //   提示：使用32位并行加法器子电路、桶形移位器、ALU控制子电路实现32位ALU
  //   功能说明:32位ALU，输入32位操作数A、B，4位控制信号ALUctr，输出32位结果Reseult和1位Zero标志位
  //   输出引脚
  //   操作数和结果
endmodule

module ALUctrl (
  input  [3:0] ALUctr,
  output SUBctr,
  output SFTctr,
  output SIGctr,
  output ALctr,
  output [2:0] OPctr
);


  // Other names for the same wires on the sheet: LRctr = SFTctr

  // Notes on the sheet:
  //   输入引脚
  //   ALU操作控制信号生成部件
  //   输出引脚
endmodule

module Adder32 (
  input  Cin,
  input  [31:0] X,
  input  [31:0] Y,
  output CF,
  output Cout,
  output OF,
  output SF,
  output [31:0] S,
  output ZF
);

  // Probe on X
  // Probe on Y
  // Probe on S

  // Notes on the sheet:
  //   Y: pull=down
  //   Cin: pull=down
  //   X: pull=down
  //   输入引脚区
  //   输出引脚区
  //   请勿修改引脚名称、电路名称及电路封装外观
  //   提示：使用16位并行加法器子电路实现32位快速加法器
  //   功能说明:32位Adder  S=X+Y，Cout为最高位进位位，Cin为进位输入， S为和，溢出OF、进位CF、零ZF、符号SF。
  //   +
  //   =
  //   无符号加法
endmodule

// 移位器
module Shifter32 (
  input  [4:0] shamt,
  input  L_R,
  input  A_L,
  input  [31:0] DataIn,
  output [31:0] DataOut
);


  // Other names for the same wires on the sheet: Arth_Logic = A_L; Din[31:0] = DataIn; Dout[31:0] = DataOut;
  //   Left_Right = L_R

  // Notes on the sheet:
  //   L/R,A/L: 00逻辑右移，01算术右移，10逻辑左移，11：循环左移
  //   输入引脚
  //   请勿修改引脚名称、电路名称及电路封装外观
  //   提示：使用多路选择器、逻辑门实现32位桶形移位器，禁止直接使用移位器组件。
  //   输出引脚
endmodule

module Adder16 (
  input  C0,
  input  [15:0] X,
  input  [15:0] Y,
  output C16,
  output Pg,
  output Gg,
  output [15:0] S
);

  // Probe on X
  // Probe on Y
  // Probe on S

  // Notes on the sheet:
  //   X: pull=down
  //   Y: pull=down
  //   C0: pull=down
  //   输入引脚区
  //   请勿修改引脚名称、电路名称及电路封装外观
  //   提示：使用4位先行进位加法器和CLU子电路实现16位并行加法器
  //   功能说明:16位Adder  S=X+Y，C16为最高位进位位，C0为进位输入， Pg、Gg为成组进位生成传递函数
  //   输出引脚区
  //   +
  //   =
  //   无符号加法
endmodule

module CLA4 (
  input  [3:0] X,
  input  [3:0] Y,
  input  Cin,
  output [3:0] F,
  output Cout,
  output Pg,
  output Gg
);

  Hex_Digit_Display hex_digit_display_1 (.value(X));  // open: dp
  Hex_Digit_Display hex_digit_display_2 (.value(Y));  // open: dp
  Hex_Digit_Display hex_digit_display_3 (.value(F));  // open: dp

  // Other names for the same wires on the sheet: Z[3:0] = F

  // Notes on the sheet:
  //   +
  //   =
  //   输出
  //   输入
  //   请勿修改引脚名称、电路名称及电路封装外观
  //   提示：使用全加器和CLU子电路实现四位先行进位加法器CLA4
endmodule

module CLU4 (
  input  P0,
  input  P1,
  input  P2,
  input  P3,
  input  G0,
  input  G1,
  input  G2,
  input  G3,
  input  C0,
  output C1,
  output C3,
  output C2,
  output C4,
  output Pg,
  output Gg
);


  // Notes on the sheet:
  //   输入引脚
  //   请勿修改引脚名称、电路名称及电路封装外观
  //   提示：使用逻辑门电路实现4位四位先行进位部件CLU，Pg、Gg为成组进位生成传递函数
  //   输出引脚
endmodule

module FA (
  input  A,
  input  B,
  input  Cin,
  output F,
  output P,
  output G
);


  // Notes on the sheet:
  //   输入引脚
  //   请勿修改引脚名称、电路名称及电路封装外观
  //   输出引脚
endmodule

module \xor  (
  input  in_1,
  input  in_2,
  input  in_3,
  output out_4
);

  wire and_1_out, and_2_out, and_3_out;

  and and_1 (and_1_out, ~in_1, in_2, in_3);  // AND_Gate
  or or_1 (out_4, and_1_out, and_2_out, and_3_out);
  and and_2 (and_2_out, in_1, ~in_2, in_3);  // AND_Gate
  and and_3 (and_3_out, in_1, in_2, ~in_3);  // AND_Gate
endmodule
