// Logisim project 2-1MUX-2_tst.circ as structural Verilog: 1 circuit, main circuit test
module test (
  output [3:0] Cnt,
  output [2:0] SD0D1,
  output F,
  output _passed,
  output halt
);

  wire CLK, FS, Running;

  Clock clock_1 (.out(CLK));
  Counter #(.width(4), .max('hf), .behavior("old")) counter_1 (
    .count(Running), .Q(Cnt), .clk(CLK));  // open: load, D, carry, clr, preset
  // Probe on Cnt
  // Probe on Cnt
  // Probe on 4'b0111
  Comparator #(.width(4)) comparator_1 (.a(Cnt), .b(4'b0111), .eq(halt));  // open: gt, lt
  ROM #(.addrWidth(4), .dataWidth(3), .Select("high")) rom_1 (.addr(Cnt), .data(SD0D1));
  not not_1 (Running, halt);
  RAM #(.addrWidth(4), .dataWidth(1), .bus("separate"), .Select("low")) ram_1 (
    .addr(Cnt), .din(F), .str(Running), .clk(CLK));  // open: data, sel, ld, clr
  _2_1MUX_2_main main_1 (.D0(SD0D1[1]), .D1(SD0D1[0]), .S(SD0D1[2]), .Y(F));
  _2_1MUXstd_main main_2 (.D0(SD0D1[1]), .D1(SD0D1[0]), .S(SD0D1[2]), .Y(FS));
  xnor xnor_1 (_passed, F, FS);
  Pull_Resistor pull_resistor_1 (.node(_passed));

  // Other names for the same wires on the sheet: Equal = _passed; tunnel[3:0] = Cnt

  // Notes on the sheet:
  //   测试节拍数
  //   contents of rom_1 (hex, n*v repeats v):
  //   0 1 2 3 4 5 6 7
endmodule
