// Logisim project 4-1MUX_tst.circ as structural Verilog: 1 circuit, main circuit test
module test (
  output [3:0] Cnt,
  output [5:0] SD,
  output F,
  output _passed,
  output halt
);

  wire CLK, FS, Running;

  Clock clock_1 (.out(CLK));
  Counter #(.width(4), .max('hf), .behavior("old")) counter_1 (
    .count(Running), .Q(Cnt), .clk(CLK));  // open: load, D, carry, clr, preset
  // Probe on Cnt
  // Probe on Cnt
  // Probe on 4'b0011
  Comparator #(.width(4)) comparator_1 (.a(Cnt), .b(4'b0011), .eq(halt));  // open: gt, lt
  ROM #(.addrWidth(4), .dataWidth(6), .Select("high")) rom_1 (.addr(Cnt), .data(SD));
  not not_1 (Running, halt);
  RAM #(.addrWidth(4), .dataWidth(1), .bus("separate"), .Select("low")) ram_1 (
    .addr(Cnt), .din(F), .str(Running), .clk(CLK));  // open: data, sel, ld, clr
  _4_1MUX_main main_1 (.D0(SD[0]), .D1(SD[1]), .D2(SD[2]), .D3(SD[3]), .S0(SD[4]), .S1(SD[5]), .Y(F));
  _4_1MUXstd_main main_2 (.D0(SD[0]), .D1(SD[1]), .D2(SD[2]), .D3(SD[3]), .S0(SD[4]), .S1(SD[5]), .Y(FS));
  xnor xnor_1 (_passed, F, FS);
  Pull_Resistor pull_resistor_1 (.node(_passed));

  // Other names for the same wires on the sheet: Equal = _passed; tunnel[3:0] = Cnt

  // Notes on the sheet:
  //   测试节拍数
  //   contents of rom_1 (hex, n*v repeats v):
  //   1 12 24 38
endmodule
