// Logisim project 4-1MUXstd.circ as structural Verilog: 2 circuits, main circuit main
module main (
  input  D0,
  input  D1,
  input  D2,
  input  D3,
  input  S0,
  input  S1,
  output Y
);

  wire _2_1MUX_2_y, _2_1MUX_y;

  _2_1MUX _2_1MUX (.D0(D0), .D1(D1), .S(S0), .Y(_2_1MUX_y));
  _2_1MUX _2_1MUX_2 (.D0(D2), .D1(D3), .S(S0), .Y(_2_1MUX_2_y));
  _2_1MUX _2_1MUX_3 (.D0(_2_1MUX_y), .D1(_2_1MUX_2_y), .S(S1), .Y(Y));
endmodule

module _2_1MUX (
  input  D0,
  input  D1,
  input  S,
  output Y
);

  wire transistor_1_out;

  Transistor transistor_1 (.in(1'b1), .out(transistor_1_out), .gate(S));
  Transistor #(.\type ("n")) transistor_2 (.in(1'b0), .out(transistor_1_out), .gate(S));
  // Transmission_Gate transmission_1: pin names not known; wires that end beside it: D0, S, transistor_1_out, Y
  // Transmission_Gate transmission_2: pin names not known; wires that end beside it: D1, transistor_1_out, S, Y

  // Notes on the sheet:
  //   2选1多路选择器
endmodule
