// Logisim project BoolExprTest.circ as structural Verilog: 1 circuit, main circuit Test
module Test (
  output [3:0] Cnt,
  output [2:0] ABC,
  output F,
  output _passed,
  output halt
);

  wire CLK, FS, Running;

  Clock #(.highDuration(1), .lowDuration(1)) clock_1 (.out(CLK));
  Counter #(.width(4), .max('hf), .ongoal("wrap"), .trigger("rising"), .behavior("old")) counter_1 (
    .count(Running), .Q(Cnt), .clk(CLK));  // open: load, D, carry, clr, preset
  // Probe on Cnt
  // Probe on Cnt
  // Probe on 4'b0111
  Comparator #(.width(4), .mode("twosComplement")) comparator_1 (.a(Cnt), .b(4'b0111), .eq(halt));  // open: gt, lt
  ROM #(.addrWidth(4), .dataWidth(3), .Select("high")) rom_1 (.addr(Cnt), .data(ABC));
  ROM #(.addrWidth(4), .dataWidth(1), .Select("high")) rom_2 (.addr(Cnt), .data(FS));
  not not_1 (Running, halt);
  RAM #(.addrWidth(4), .dataWidth(1), .bus("separate"), .Select("low")) ram_1 (
    .addr(Cnt), .din(F), .str(Running), .clk(CLK));  // open: data, sel, ld, clr
  \布尔表达式  \u_布尔表达式_1  (.A(ABC[0]), .B(ABC[1]), .C(ABC[2]), .F(F));
  xnor xnor_1 (_passed, F, FS);
  Pull_Resistor #(.pull(0)) pull_resistor_1 (.node(_passed));

  // Other names for the same wires on the sheet: Equal = _passed; tunnel[3:0] = Cnt

  // Notes on the sheet:
  //   测试节拍数
  //   contents of rom_1 (hex, n*v repeats v):
  //   0 1 2 3 4 5 6 7
  //   contents of rom_2 (hex, n*v repeats v):
  //   0 0 0 1 0 1 1 1
endmodule
