// Logisim project Decoder3to8_test.circ as structural Verilog: 2 circuits, main circuit main
module main (
);

  wire and_1_out, clk, comparator_1_eq, d_ff_1_qn, halt, NEQ, not_1_out;
  wire [5:0] counter_1_q, counter_2_q, data;
  wire [7:0] main_1_y0_l, n74x138_1_y0_l;

  Clock clock_1 (.out(clk));
  not not_1 (not_1_out, halt);
  Counter #(.width(6), .max('h3f)) counter_1 (
    .count(not_1_out), .Q(counter_1_q), .carry(halt), .clk(clk));  // open: load, D, clr, preset, down
  LED led_1 (.in(halt));
  Counter #(.width(6), .max('h3f), .behavior("old")) counter_2 (
    .count(NEQ), .Q(counter_2_q), .clk(clk), .clr(halt));  // open: load, D, carry, preset
  ROM #(.addrWidth(6), .dataWidth(6), .Select("low")) rom_1 (.addr(counter_1_q), .data(data));
  and and_1 (and_1_out, ~halt, NEQ);  // AND_Gate
  Decoder3to8_main main_1 (
    .A(data[0]), .G1(data[5]), .Y0_L(main_1_y0_l[0]), .Y4_L(main_1_y0_l[4]), .B(data[1]), .G2A_L(data[4]),
    .Y1_L(main_1_y0_l[1]), .Y5_L(main_1_y0_l[5]), .C(data[2]), .G2B_L(data[3]), .Y2_L(main_1_y0_l[2]),
    .Y6_L(main_1_y0_l[6]), .Y3_L(main_1_y0_l[3]), .Y7_L(main_1_y0_l[7]));
  RAM #(.addrWidth(6), .dataWidth(6), .bus("separate"), .Select("low")) ram_1 (
    .addr(counter_2_q), .din(data), .str(and_1_out), .clk(clk));  // open: data, sel, ld, clr
  _74X138 u_74x138_1 (
    .G1(data[5]), .G2A_L(data[4]), .G2B_L(data[3]), .A(data[0]), .B(data[1]), .C(data[2]),
    .Y0_L(n74x138_1_y0_l[0]), .Y0_L_2(n74x138_1_y0_l[1]), .Y0_L_3(n74x138_1_y0_l[2]),
    .Y0_L_4(n74x138_1_y0_l[3]), .Y0_L_5(n74x138_1_y0_l[4]), .Y0_L_6(n74x138_1_y0_l[5]),
    .Y0_L_7(n74x138_1_y0_l[6]), .Y0_L_8(n74x138_1_y0_l[7]));
  D_Flip_Flop #(.enable("true")) d_ff_1 (.clk(clk), .D(NEQ), .Qn(d_ff_1_qn), .en(d_ff_1_qn));  // open: Q, preset, reset
  not not_2 (NEQ, comparator_1_eq);
  Comparator comparator_1 (.a(n74x138_1_y0_l), .b(main_1_y0_l), .eq(comparator_1_eq));  // open: gt, lt

  // Notes on the sheet:
  //   contents of rom_1 (hex, n*v repeats v):
  //   0 1 2 3 4 5 6 7 8 9 a b c d e f 10 11 12 13 14 15 16 17 18 19 1a 1b 1c 1d 1e 1f 20 21 22 23 24 25 26
  //   27 28 29 2a 2b 2c 2d 2e 2f 30 31 32 33 34 35 36 37 38 39 3a 3b 3c 3d 3e 3f
endmodule

module _74X138 (
  input  G1,
  input  G2A_L,
  input  G2B_L,
  input  A,
  input  B,
  input  C,
  output Y0_L,
  output Y0_L_2,
  output Y0_L_3,
  output Y0_L_4,
  output Y0_L_5,
  output Y0_L_6,
  output Y0_L_7,
  output Y0_L_8
);

  wire and_1_out, not_1_out, not_2_out, not_3_out, not_4_out, not_5_out, not_6_out, not_7_out;

  not not_1 (not_1_out, G1);
  and and_1 (and_1_out, ~not_1_out, ~G2A_L, ~G2B_L);  // AND_Gate
  not not_2 (not_2_out, A);
  not not_3 (not_3_out, B);
  not not_4 (not_4_out, C);
  not not_5 (not_5_out, not_2_out);
  not not_6 (not_6_out, not_3_out);
  not not_7 (not_7_out, not_4_out);
  nand nand_1 (Y0_L, not_2_out, not_3_out, not_4_out, and_1_out);
  nand nand_2 (Y0_L_2, not_5_out, not_3_out, not_4_out, and_1_out);
  nand nand_3 (Y0_L_3, not_2_out, not_6_out, not_4_out, and_1_out);
  nand nand_4 (Y0_L_4, not_5_out, not_6_out, not_4_out, and_1_out);
  nand nand_5 (Y0_L_5, not_2_out, not_3_out, not_7_out, and_1_out);
  nand nand_6 (Y0_L_6, not_5_out, not_3_out, not_7_out, and_1_out);
  nand nand_7 (Y0_L_7, not_2_out, not_6_out, not_7_out, and_1_out);
  nand nand_8 (Y0_L_8, and_1_out, not_5_out, not_6_out, not_7_out);
endmodule
