// Logisim project InstrToImm_test.circ as structural Verilog: 2 circuits, main circuit main
module main (
  output [31:0] Instr,
  output [2:0] Extop,
  output [31:0] Imm,
  output halt,
  output _passed
);

  wire clk, halt1, halt2, not_1_out, not_2_out;
  wire [1:0] counter_1_q, counter_2_q;
  wire [31:0] instrtoimm_2_imm;

  not not_1 (not_1_out, halt2);
  Counter #(.width(2), .max('h3)) counter_1 (
    .count(not_1_out), .Q(counter_1_q), .carry(halt2), .clk(clk));  // open: load, D, clr, preset, down
  Clock clock_1 (.out(clk));
  ROM #(.addrWidth(2), .dataWidth(32), .Select("low")) rom_1 (.addr(counter_1_q), .data(Instr));
  InstrToImm instrtoimm_1 (.Instr(Instr), .Extop(Extop), .imm(Imm));
  IFU_InstrToImm instrtoimm_2 (.Instr(Instr), .Extop(Extop), .imm(instrtoimm_2_imm));
  not not_2 (not_2_out, halt1);
  Counter #(.width(2), .max('h3)) counter_2 (
    .count(not_2_out), .Q(counter_2_q), .carry(halt1), .clk(clk));  // open: load, D, clr, preset, down
  ROM #(.addrWidth(2), .dataWidth(3), .Select("low")) rom_2 (.addr(counter_2_q), .data(Extop));
  Comparator #(.width(32)) comparator_1 (.a(Imm), .b(instrtoimm_2_imm), .eq(_passed));  // open: gt, lt
  and and_1 (halt, halt1, halt2);

  // Other names for the same wires on the sheet: Equal = _passed

  // Notes on the sheet:
  //   contents of rom_1 (hex, n*v repeats v):
  //   12b7 fff28293 5de1863 288000ef
  //   contents of rom_2 (hex, n*v repeats v):
  //   1 0 3 4
endmodule

module InstrToImm (
  input  [31:0] Instr,
  input  [2:0] Extop,
  output [31:0] imm
);

  wire [11:0] bit_extender_4_out;
  wire [19:0] bit_extender_1_out, bit_extender_2_out, bit_extender_3_out;

  assign bit_extender_1_out = {{19{Instr[31]}}, Instr[31]};  // Bit_Extender bit_extender_1
  assign bit_extender_2_out = {{19{Instr[31]}}, Instr[31]};  // Bit_Extender bit_extender_2
  assign bit_extender_3_out = {{19{Instr[31]}}, Instr[31]};  // Bit_Extender bit_extender_3
  assign bit_extender_4_out = {{11{Instr[31]}}, Instr[31]};  // Bit_Extender bit_extender_4
  Multiplexer #(.select(3), .width(32), .enable("false")) multiplexer_1 (
    .in0({bit_extender_1_out, Instr[31:20]}), .in1({Instr[31:12], {12{1'b0}}}),
    .in2({bit_extender_2_out, Instr[31:25], Instr[11:7]}),
    .in3({bit_extender_3_out, Instr[7], Instr[30:25], Instr[11:8], 1'b0}),
    .in4({bit_extender_4_out, Instr[19:12], Instr[20], Instr[30:21], 1'b0}), .in5({32{1'b0}}),
    .in6({32{1'b0}}), .in7({32{1'b0}}), .out(imm), .sel(Extop));

  // Notes on the sheet:
  //   Extop: pull=down
  //   Instr: pull=down
  //   I
  //   U
  //   S
  //   B
  //   J
  //   输入引脚
  //   输出引脚
endmodule
